// Digital circuit MUX_74151.dig as structural Verilog
module MUX_74151 (
  input  D,
  input  C,
  input  B,
  input  A,
  output Y
);

  wire _74151_1_pin7, _74151_1_pin13;

  _74151 _74151_1 (
    .pin1(D), .pin2(D), .pin3(D), .pin4(1'b1), .pin5(Y), .pin7(_74151_1_pin7), .pin8(_74151_1_pin7),
    .pin9(C), .pin10(B), .pin11(A), .pin12(_74151_1_pin7), .pin13(_74151_1_pin13), .pin14(_74151_1_pin13),
    .pin15(_74151_1_pin13), .pin16(1'b1));  // open: pin6
  not not_1 (_74151_1_pin13, D);

  // Notes on the sheet:
  //   74151 Multiplexer:
  //   C,B,A are select bits.  C is the MSB.
  //   D0-D7 are input data lines
  //   Y is the output
  //   W is the inverted output
  //   S is strobe.  When strobe is high the output is always low, 
  //     otherwise it's the selected data line.
  //   Inputs: Use A as the most-significant bit and 
  //   D as the least-significant bit.
endmodule

/* Test case:
A B C D Y
0 0 0 0 X
0 0 0 1 1
*/
